# Fritzing sketch project (saved by Fritzing 0.9.3b)
breadboards: 2

parts:
  Part3 = Arduino Mega 2560 (Rev3)
  R1 = PHOTOCELL [package=photocell]
  R2 = Resistor [tolerance=±5% resistance=220 package="1206 [SMD]"]
  R3 = Resistor [tolerance=±5% resistance=09.1k package="0402 [SMD]"]
  LED1 = smd LED [color="Red (633nm)" package="1206 [SMD]"]  # not connected
  L298N1 = L298N DC motor driver
  M1 = DC Motor
  M2 = DC Motor
  VCC1 = Battery
  Part4 = KY-033 Tracing Black White Line Hunting Sensor Module For Arduino
  Part5 = KY-033 Tracing Black White Line Hunting Sensor Module For Arduino
  DI1 = 7-Segment LED Display [package=THT]
  Mod1 = KY-023 Dual Axis Joystick Module [package="Breakout board"]
  R4 = Resistor [tolerance=±5% resistance=220 package="1206 [SMD]"]
  R5 = Resistor [tolerance=±5% resistance=220 package="1206 [SMD]"]
  R7 = Resistor [tolerance=±5% resistance=220 package="1206 [SMD]"]
  R8 = Resistor [tolerance=±5% resistance=220 package="1206 [SMD]"]
  R9 = Resistor [tolerance=±5% resistance=220 package="1206 [SMD]"]
  R10 = Resistor [tolerance=±5% resistance=220 package="1206 [SMD]"]
  R11 = Resistor [tolerance=±5% resistance=220 package="1206 [SMD]"]
  Part6 = Arduino Uno (Rev3) - ICSP
  DFRobot_DFPlayer_Mini1 = DFRobot DFPlayer Mini [part_number=DFR0299]
  SP1 = SPEAKER [package=pcb_mount_speaker]
  LCD1 = elegoo-2.8in-tft-display
  R12 = Resistor [tolerance=±5% resistance=1k package="1206 [SMD]"]
  J1 = Piezo Speaker

nets:
  N1: Part3.A1, R1.P$1, R3.Pin_0
  N2: Part3.D13_PWM, Mod1.VRy
  N3: Part3.D12_PWM, Mod1.VRx
  N4: Part3.D11_PWM, Part3.D9_PWM, R5.Pin_0, R7.Pin_1, R8.Pin_1
  N5: Part3.D10_PWM, R10.Pin_0, R11.Pin_1
  N6: Part3.D8_PWM, R4.Pin_0, R9.Pin_0
  5V: Part3.5V, R1.P$2, Part4.V+, Part5.V+, Mod1.+5V
  GND: Part3.GND, R2.Pin_0, R3.Pin_1, Part4.GND, Part5.GND, DI1.commAnode#2, Mod1.GND, J1.pin1
  N7: Part3.D2_PWM, J1.pin2
  N8: Part3.D3_PWM, L298N1.5V
  N9: Part3.D4_PWM, L298N1.IN4
  N10: Part3.D5_PWM, L298N1.IN3
  N11: Part3.D6_PWM, L298N1.IN2
  N12: Part3.D7_PWM, L298N1.IN1
  N13: Part3.D22, Part4.S
  N14: Part3.D23, Part5.S
  N15: L298N1.OUT1, M1.pin_2
  N16: L298N1.OUT2, M1.pin_1
  N17: L298N1.OUT3, M2.pin_2
  N18: L298N1.OUT4, M2.pin_1
  N19: L298N1.12V, VCC1.+
  N20: L298N1.GND, VCC1.-
  N21: DI1.cathodeE, R9.Pin_1
  N22: DI1.cathodeD, R10.Pin_1
  N23: DI1.cathodeC, R11.Pin_0
  N24: DI1.cathodeB, R8.Pin_0
  N25: DI1.cathodeA, R7.Pin_0
  N26: DI1.cathodeF, R5.Pin_1
  N27: DI1.cathodeG, R4.Pin_1
  N28: Part6.A0, LCD1.LCD_RD
  N29: Part6.A1, LCD1.LCD_WR
  N30: Part6.A2, LCD1.LCD_RS
  N31: Part6.A3, LCD1.LCD_CS
  N32: Part6.A4/SDA, LCD1.LCD_RST
  N33: Part6.D8, LCD1.LCD_D0
  N34: Part6.D9_PWM, LCD1.LCD_D1
  N35: Part6.D10_PWM/SS, DFRobot_DFPlayer_Mini1.TX
  N36: Part6.D11_PWM/MOSI, R12.Pin_0
  N37: Part6.D2, LCD1.LCD_D2
  N38: Part6.D3_PWM, LCD1.LCD_D3
  N39: Part6.D4, LCD1.LCD_D4
  N40: Part6.D5_PWM, LCD1.LCD_D5
  N41: Part6.D6_PWM, LCD1.LCD_D6
  N42: Part6.D7, LCD1.LCD_D7
  N43: Part6.RESET, LCD1.NU
  3V3: Part6.3V3, LCD1.3V3
  5V_2: Part6.5V, DFRobot_DFPlayer_Mini1.VCC, LCD1.5V
  GND_2: Part6.GND, DFRobot_DFPlayer_Mini1.GND-1, DFRobot_DFPlayer_Mini1.GND-2, LCD1.GND
  N44: DFRobot_DFPlayer_Mini1.RX, R12.Pin_1
  N45: DFRobot_DFPlayer_Mini1.SPK_1, SP1.-
  N46: DFRobot_DFPlayer_Mini1.SPK_2, SP1.+

custom parts:
  L298N DC motor driver: 2x DC motor driver with 78M05 positive voltage regulator (7..35 V) L298N: max 46 V, 2 A Set 5 V Enable jumper to enable 5 V regultor (needed for the L298N) and +5 V output at screw terminal or supply external +5 V at screw terminal Set ENA and/or ENB to +5 V to enable motor permanently or supply ENA and/or ENB with PWM signal IN1 and IN2 set rotation directory for motor A (OUT1/OUT2) IN2 and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
  Battery: Your standard 3x 18650 battery pack (11.1 Volts)
  KY-033 Tracing Black White Line Hunting Sensor Module For Arduino: Tracing Black White Line Hunting Sensor Module For Arduino Description: This is KY-033 tracking sensor. The KY-033 measures the intensity of infrared radiation and delivers it as an analog output voltage. Features: Operating voltage: 2.5 - 12V(cannot over12V) working current: 18mA-20mA at 5V Enhanced accuracy Documents: http://www.vishay.com/docs/83760/tcrt5000.pdf
  KY-023 Dual Axis Joystick Module: KY-023 Dual-Axis Joystick Module.
  elegoo-2.8in-tft-display: 2.8 Inch TFT LCD Touch Screen with SD Card Socket. 240*320 pixels RGB. 4 chip white LED backlight.
